# Fritzing sketch MotionTempSensor (saved by Fritzing 0.9.3b)
breadboards: 1

parts:
  WeMos_D1_Mini1 = WeMos D1 Mini
  R1 = Temperature Sensor (Thermistor) [thermistor_type=NTC package=THT]
  R2 = Resistor [tolerance=±5% resistance=10k package=THT]
  PIR1 = PIR sensor

nets:
  N1: WeMos_D1_Mini1.3V3, R1.pin_1
  5V: WeMos_D1_Mini1.5V, PIR1.VDD
  N2: WeMos_D1_Mini1.D5, PIR1.SIG
  N3: R1.pin_0, R2.Pin_0
  N4: R2.Pin_1, PIR1.GND
